// Logisim project FSM_first_implementation.circ as structural Verilog: 4 circuits, main circuit main
module main (
);

  wire clock_1_out, fsm_1_out_green, fsm_1_out_red, fsm_1_out_yellow, I_Button_out;

  Button I_Button (.out(I_Button_out));
  Clock clock_1 (.out(clock_1_out));
  fsm fsm_1 (
    .Button(I_Button_out), .clk(clock_1_out), .Out_Red(fsm_1_out_red), .Out_Yellow(fsm_1_out_yellow),
    .Out_Green(fsm_1_out_green));
  LED Red (.in(fsm_1_out_red));
  LED Yellow (.in(fsm_1_out_yellow));
  LED Green (.in(fsm_1_out_green));
endmodule

module fsm (
  input  Button,
  input  clk,
  output Out_Red,
  output Out_Yellow,
  output Out_Green
);

  wire fsm_tl_1_d0, fsm_tl_1_d1, state_Register_2_q, stateRegister_1_q;

  fsm_tl fsm_tl_1 (.B(Button), .C1(stateRegister_1_q), .C0(state_Register_2_q), .D1(fsm_tl_1_d1), .D0(fsm_tl_1_d0));
  D_Flip_Flop stateRegister_1 (.D(fsm_tl_1_d1), .clk(clk), .Q(stateRegister_1_q));  // open: Qn, preset, reset
  D_Flip_Flop state_Register_2 (.D(fsm_tl_1_d0), .clk(clk), .Q(state_Register_2_q));  // open: Qn, preset, reset
  fsm_ol fsm_ol_1 (
    .C1(stateRegister_1_q), .C0(state_Register_2_q), .Red(Out_Red), .Yellow(Out_Yellow), .Green(Out_Green));
endmodule

module fsm_tl (
  input  B,
  input  C1,
  input  C0,
  output D1,
  output D0
);

  wire and_1_out, and_2_out, not_1_out, not_2_out, not_3_out;

  not not_1 (not_1_out, C1);
  not not_2 (not_2_out, C0);
  not not_3 (not_3_out, C0);
  and and_1 (and_1_out, not_1_out, C0);
  and and_2 (and_2_out, C1, not_2_out);
  and and_3 (D0, B, not_3_out);
  or or_1 (D1, and_1_out, and_2_out);
endmodule

module fsm_ol (
  input  C1,
  input  C0,
  output Red,
  output Yellow,
  output Green
);

  wire not_1_out, not_2_out;

  not not_1 (not_1_out, C1);
  not not_2 (not_2_out, C0);
  and and_1 (Green, not_1_out, not_2_out);

  assign Red = C1;
  assign Yellow = C0;
endmodule
